# Fritzing sketch lueftung (saved by Fritzing 1.0.1rc)
circuit board: 8.79866cm x 5.51789cm
breadboards: 1

parts:
  JP1 = Header 6 [package=molex-1x6_lock]  # not connected
  JP2 = Header 6 [package=molex-1x6_lock]  # not connected
  J2 = Camdenboss CTB0158-2 [part_number=CTB0158-2 package=THT]
  J5 = Camdenboss CTB0158-3 [part_number=CTB0158-3 package=THT]
  J3 = Camdenboss CTB0158-3 [part_number=CTB0158-3 package=THT]
  J1 = Camdenboss CTB0158-3 [part_number=CTB0158-3 package=THT]
  J4 = Camdenboss CTB0158-3 [part_number=CTB0158-3 package=THT]
  U2 = Mini-360 DC-DC Buck converter [package=THT]
  U1 = LuaNode32 / ESP32 [part_number=ESP32S-PIN30]
  R1 = Resistor [tolerance=±5% resistance=10k power=0.25 package=THT]
  R2 = Resistor [tolerance=±5% resistance=10k power=0.25 package=THT]
  Bauteil1 = Adafruit 4-channel I2C-safe Bi-directional Logic Level Converter [part_number="Adafruit #757"]
  J6 = female pin header, 6 pins [form="♀ (female)"]
  J7 = female pin header, 2 pins [form="♀ (female)"]
  J8 = female pin header, 4 pins [form="♀ (female)"]

nets:
  N1: J2.pin1, J5.pin1, J3.pin1, J1.pin1, J4.pin1, U2.IN-
  N2: J2.pin2, J5.pin3, J3.pin3, J1.pin3, J4.pin3, U2.IN+
  N3: J5.pin2, U1.D26, Bauteil1.GND
  N4: J3.pin2, Bauteil1.B1
  N5: J1.pin2, Bauteil1.HV
  N6: J4.pin2, Bauteil1.B4
  N7: U2.OUT+, U1.Vin, Bauteil1.B3, J8.pin3, J8.pin4
  N8: U2.OUT-, U1.GND, R1.Pin_0, R2.Pin_1, Bauteil1.A2, Bauteil1.B2, J7.pin1
  N9: U1.D34, R2.Pin_0, J8.pin1
  N10: U1.D32, Bauteil1.LV
  N11: U1.D33, Bauteil1.A1
  N12: U1.D25, Bauteil1.A4
  N13: U1.D27, J6.pin1
  N14: U1.D14, J6.pin2
  N15: U1.3V3, Bauteil1.A3, J7.pin2
  N16: U1.D4, J6.pin6
  N17: U1.D21, J6.pin5
  N18: U1.D22, J6.pin4
  N19: U1.D23, J6.pin3
  N20: R1.Pin_1, J8.pin2

custom parts:
  Mini-360 DC-DC Buck converter: Mini-360 DC-DC Buck converter. Tiny buck step down voltage converter, input voltage 4.75 to 23V output 1 to 17V adjustable. Available from ebay and the like.
  LuaNode32 / ESP32: New Image for LuaNode32 DOIT ESP32 DEVKIT V1. Base parts from LuaNode32 / ESP32 ESP32 based LuaNode32 by G.Noorlander DOIT Esp32 DevKit v1 (30 pins long, 11 pins width) by Werner Rothschopf (modified by vanepp Dec 2018)
  Adafruit 4-channel I2C-safe Bi-directional Logic Level Converter: Because the Arduino (and Basic Stamp) are 5V devices, and most modern sensors, displays, flash cards and modes are 3.3V-only, many makers find that they need to perform level shifting/conversion to protect the 3.3V device from 5V. We do have some other handy level shifters in the shop, from the DIP 74LVC245 to the fancy bi-directional TXB0108. However, neither of these are happy to work with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
